# Fritzing sketch Fan Control (saved by Fritzing 0.9.3b)
circuit board: 1.85766cm x 1.53949cm
breadboards: 1

parts:
  5V_R1 = Resistor [tolerance=±5% resistance=1k package=THT]
  3V_R1 = Resistor [tolerance=±5% resistance=1k package=THT]
  3V_R2 = Resistor [tolerance=±5% resistance=169 package=THT]
  BC640 = PNP-Transistor [package="TO92 [THT]"]
  BC639 = NPN-Transistor [package="TO92 [THT]"]
  Diode = Resistor [tolerance=±5% resistance=0 package=THT]
  BC639_2 = NPN-Transistor [package="TO92 [THT]"]
  Fan = DC Motor
  BC640_2 = PNP-Transistor [package="TO92 [THT]"]
  Raspberry_Pi = Raspberry Pi 3 [part_number=RPI-3-V1.2]
  5V_R2 = Resistor [tolerance=±5% resistance=169 package=THT]

nets:
  N1: 5V_R1.Pin_0, BC639_2.B
  N2: 5V_R1.Pin_1, Raspberry_Pi.GPIO17
  N3: 3V_R1.Pin_0, BC639.B
  N4: 3V_R1.Pin_1, Raspberry_Pi.GPIO18
  N5: 3V_R2.Pin_0, BC639.E
  N6: 3V_R2.Pin_1, BC640_2.B
  3V3: BC640.E, Raspberry_Pi.3v3, Raspberry_Pi.3V3
  N7: BC640.B, 5V_R2.Pin_0
  N8: BC640.C, Diode.Pin_1, BC640_2.C
  N9: BC639.C, Diode.Pin_0, BC639_2.C, Fan.pin_2, Raspberry_Pi.GND
  N10: BC639_2.E, 5V_R2.Pin_1
  N11: BC640_2.E, Raspberry_Pi.5V

notes:
  5V
  C5
  3V
  C3
  G
  V-
  V+
  BC639
  640
  169Ω
  639
